# Fritzing sketch wiring_diagram (saved by Fritzing 0.9.9b)
breadboards: 1

parts:
  U1 = ESP32S-HiLetgo [part_number=ESP32S-HiLetgo]
  ANT1 = Antenna
  S1 = Pushbutton [package="[THT]"]
  LED1 = LED - 5mm [color="Red (633nm)" current=0.030 package="5 mm [THT]"]
  R3 = Resistor [tolerance=±5% resistance=220 package="1206 [SMD]"]
  R4 = Resistor [tolerance=±5% resistance=220 package="1206 [SMD]"]
  R5 = Rotary Potentiometer (Small) [maximum_resistance=10kΩ package=THT]

nets:
  N1: U1.3.3, U1.GPIO12, S1.Pin_1, S1.Pin_2, R5.leg1
  N2: U1.GPIO14, LED1.anode
  N3: U1.GND, R3.Pin_1, R4.Pin_0
  N4: U1.GPIO19, R4.Pin_1
  N5: U1.GPIO1, R5.wiper
  N6: ANT1.antenna_lead, R5.leg2
  N7: S1.Pin_3, S1.Pin_4
  N8: LED1.cathode, R3.Pin_0

custom parts:
  ESP32S-HiLetgo: HiLetgo ESP-WROOM-32 ESP32 ESP-32S Development Board 2.4GHz Dual-Mode WiFi + Bluetooth Dual Cores Microcontroller The ESP32 integrated with Antenna switches, RF Balun, power amplifiers, low-noise amplifiers, filters, and management modules, and the entire solution occupies the least area of PCB. 2.4 GHz Wi-Fi plus Bluetooth dual-mode chip, with TSMC Ultra-low power consumption 40nm technology,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
